# Fritzing sketch AlarmINO - v0.1 (saved by Fritzing 0.9.3b)
breadboards: 1

parts:
  ARDUINO_UNO_(REV_3) = Arduino Uno (Rev3)  # not connected
  ARDUINO_GSM_SHIELD = Arduino GSM Shield
  LED1 = LED - 5mm [color="Green (555nm)" package="5 mm [THT]"]
  LED2 = LED - 5mm [color="Red (633nm)" package="5 mm [THT]"]
  PIR_SENSOR = PIR sensor

nets:
  N1: ARDUINO_GSM_SHIELD.AGND, LED1.cathode, LED2.cathode, PIR_SENSOR.GND
  N2: ARDUINO_GSM_SHIELD.SCK/D13, LED1.anode
  N3: ARDUINO_GSM_SHIELD.MISO/D12, LED2.anode
  5V: ARDUINO_GSM_SHIELD.5V, PIR_SENSOR.VDD
  N4: ARDUINO_GSM_SHIELD.PWM_D4, PIR_SENSOR.SIG

notes:
  AllarmINO v0.1
